# Fritzing sketch Data Monitor and Alert System (saved by Fritzing 0.9.3b)
breadboards: 2

parts:
  LCD3 = LCD screen
  U1 = NodeMCU V1.0
  B2 = Bolt WiFi Module [package=dip]
  U2 = 74HC595 [package="DIP16 [THT]"]
  DHT1 = DHT22 Humidity and Temperature Sensor
  S1 = KY-026
  MQ-2 = GAS_SENSOR [package=mq-3]
  MQ-135 = GAS_SENSOR [package=mq-3]
  CD1 = CD4051
  Mod1 = KY-012 Active Buzzer Module [package="Breakout board"]
  R1 = Resistor [tolerance=±5% resistance=150 package="2512 [SMD]"]
  LED1 = LED - 5mm [color="Red (633nm)" package="5 mm [THT]"]
  LED2 = LED - 5mm [color="Red (633nm)" package="5 mm [THT]"]
  LED3 = LED - 5mm [color="Red (633nm)" package="5 mm [THT]"]
  LED4 = LED - 5mm [color="Red (633nm)" package="5 mm [THT]"]
  R2 = Resistor [tolerance=±5% resistance=150 package="2512 [SMD]"]
  R3 = Resistor [tolerance=±5% resistance=150 package="2512 [SMD]"]
  R4 = Resistor [tolerance=±5% resistance=150 package="2512 [SMD]"]
  LED5 = LED - 5mm [color="Red (633nm)" package="5 mm [THT]"]
  LED6 = LED - 5mm [color="Red (633nm)" package="5 mm [THT]"]
  R5 = Resistor [tolerance=±5% resistance=150 package="2512 [SMD]"]
  R6 = Resistor [tolerance=±5% resistance=150 package="2512 [SMD]"]
  LED7 = LED - 5mm [color="Red (633nm)" package="5 mm [THT]"]
  R7 = Resistor [tolerance=±5% resistance=150 package="2512 [SMD]"]
  LCM1602_IIC4 = LCM1602 IIC [part_number="LCM1602 IIC" chip_label="LCM1602 IIC" package="DIP (Dual Inline) [THT]"]

nets:
  VSS: LCD3.VSS, LCM1602_IIC4.VSS
  VDD: LCD3.VDD, LCM1602_IIC4.VDD
  N1: LCD3.V0, LCM1602_IIC4.V0
  N2: LCD3.RS, LCM1602_IIC4.RS
  N3: LCD3.R/W, LCM1602_IIC4.RW
  N4: LCD3.E, LCM1602_IIC4.E
  N5: LCD3.DB0, LCM1602_IIC4.D0
  N6: LCD3.DB1, LCM1602_IIC4.D1
  N7: LCD3.DB2, LCM1602_IIC4.D2
  N8: LCD3.DB3, LCM1602_IIC4.D3
  N9: LCD3.DB4, LCM1602_IIC4.D4
  N10: LCD3.DB5, LCM1602_IIC4.D5
  N11: LCD3.DB6, LCM1602_IIC4.D6
  N12: LCD3.DB7, LCM1602_IIC4.D7
  N13: LCD3.LED+, LCM1602_IIC4.A
  N14: LCD3.LED-, LCM1602_IIC4.K
  N15: U1.D0, S1.pin4
  N16: U1.D1, U2.OE, S1.pin2, MQ-135.A1, CD1.Input_C, CD1.Input_B, LED1.cathode, LED2.cathode, LED3.cathode, LED4.cathode, LED5.cathode, LED6.cathode, LED7.cathode, LCM1602_IIC4.SCL
  N17: U1.D2, MQ-2.A1, CD1.Chan_0, LCM1602_IIC4.SDA
  N18: U1.D3, Mod1.NC
  N19: U1.D4, CD1.Input_A
  VDD_2: U1.3V3, B2.pin10, U2.MR, U2.VCC, DHT1.VDD, S1.pin3, MQ-2.H1, MQ-135.B1, CD1.VDD, Mod1.S
  GND: U1.GND, B2.pin1, U2.GND, DHT1.GND, MQ-2.H2, CD1.Inhibit, CD1.VEE, CD1.VSS, Mod1.-, LCM1602_IIC4.GND
  N20: U1.D5, DHT1.DATA
  N21: U1.D6, U2.DS
  N22: U1.D7, U2.ST_CP
  N23: U1.D8, U2.SH_CP
  N24: U1.RX, B2.pin8
  N25: U1.TX, B2.pin9
  N26: U1.A0, CD1.In/Out
  N27: B2.pin11, LCM1602_IIC4.VCC
  N28: U2.Q1, R6.Pin_0
  N29: U2.Q2, R5.Pin_0
  N30: U2.Q3, R4.Pin_0
  N31: U2.Q4, R3.Pin_0
  N32: U2.Q5, R2.Pin_0
  N33: U2.Q6, R1.Pin_0
  N34: U2.Q0, R7.Pin_0
  N35: MQ-135.H1, CD1.Chan_1
  N36: R1.Pin_1, LED1.anode
  N37: LED2.anode, R2.Pin_1
  N38: LED3.anode, R3.Pin_1
  N39: LED4.anode, R4.Pin_1
  N40: LED5.anode, R5.Pin_1
  N41: LED6.anode, R6.Pin_1
  N42: LED7.anode, R7.Pin_1

custom parts:
  NodeMCU V1.0: ESP8266 based NodeMCU
  Bolt WiFi Module: Bolt IoT platform gives you the capability to control your devices and collect data from IoT devices safely and securely no matter where you are. Get actionable insights by deploying machine learning algorithms with just a few clicks to detect anomalies as well as predict sensor values.
  KY-026: ky-026 flame sensor module
  KY-012 Active Buzzer Module: Active Piezoelectric Buzzer Module KY-012, it produces single-tone sound when signal is high. (Special thanks to vanepp for fixing the PCB holes and other errors)
  LCM1602 IIC: I2C-Module to use a 1602 or 2004 LCD on with the wire.h libory Serial LCD Modul
